# Fritzing sketch Opstelling_ (saved by Fritzing 0.8.7b)
circuit board: 8.46667cm x 5.64444cm
breadboards: 1

parts:
  Part1 = Arduino Uno (Rev3)
  7_Segment1 = 7 Segment Display
  R1 = Resistor [tolerance=±5% resistance=220 package=THT]
  R2 = Resistor [tolerance=±5% resistance=220 package=THT]
  R3 = Resistor [tolerance=±5% resistance=220 package=THT]
  R4 = Resistor [tolerance=±5% resistance=220 package=THT]
  R5 = Resistor [tolerance=±5% resistance=220 package=THT]
  R6 = Resistor [tolerance=±5% resistance=220 package=THT]
  R7 = Resistor [tolerance=±5% resistance=220 package=THT]
  R8 = Resistor [tolerance=±5% resistance=220 package=THT]
  U1 = 74HC595 SMD [package="SO16 [SMD]"]
  S1 = Pushbutton [package="[THT]"]
  R9 = Resistor [tolerance=±5% resistance=10k package=THT]
  Part2 = Real Time Clock Module - DS1307 RTC Breakout Board

nets:
  N1: Part1.D8, U1.DS
  N2: Part1.D9_PWM, U1.ST_CP
  N3: Part1.D10_PWM/SS, U1.SH_CP
  GND: Part1.GND, 7_Segment1.common_anode, U1.GND, U1.OE, R9.Pin_0, Part2.GND
  N4: Part1.A4/SDA, Part2.SDA
  N5: Part1.A5/SCL, Part2.SCL
  N6: Part1.D2, S1.Pin_3, S1.Pin_4, R9.Pin_1
  5V: Part1.5V, U1.MR, U1.VCC, S1.Pin_1, S1.Pin_2, Part2.5V
  N7: 7_Segment1.Segment_E, R8.Pin_1
  N8: 7_Segment1.Segment_D, R6.Pin_1
  N9: 7_Segment1.Segment_C, R5.Pin_0
  N10: 7_Segment1.Segment_DP, R7.Pin_0
  N11: 7_Segment1.Segment_B, R1.Pin_0
  N12: 7_Segment1.Segment_A, R2.Pin_0
  N13: 7_Segment1.Segment_F, R3.Pin_1
  N14: 7_Segment1.Segment_G, R4.Pin_1
  N15: R1.Pin_1, U1.Q1
  N16: R2.Pin_1, U1.Q0
  N17: R3.Pin_0, U1.Q5
  N18: R4.Pin_0, U1.Q6
  N19: R5.Pin_1, U1.Q2
  N20: R6.Pin_0, U1.Q3
  N21: R7.Pin_1, U1.Q7
  N22: R8.Pin_0, U1.Q4
